// Logisim project Registers.circ as structural Verilog: 1 circuit, main circuit Registers
module Registers (
  input  RegWrite,
  input  CLR,
  input  [3:0] WriteData,
  input  [3:0] Dst_Reg_1,
  input  CLK,
  input  [3:0] SrcReg1,
  input  [3:0] SrcReg2,
  output [3:0] Read_Data_1,
  output [3:0] Read_Data_2
);

  wire demultiplexer_1_out0, demultiplexer_1_out1, demultiplexer_1_out2, demultiplexer_1_out3,
       demultiplexer_1_out4, demultiplexer_1_out6, demultiplexer_1_out7;
  wire [2:0] and_2_out;
  wire [3:0] and_1_out, sp_q, t0_q, t1_q, t2_q, t3_q, t4_q, zero_q;

  assign and_1_out = 4'b0000 & WriteData;  // AND_Gate and_1, 4 bits wide
  Multiplexer #(.select(3), .width(4), .enable("false")) multiplexer_1 (
    .in0(zero_q), .in1(t1_q), .in2(t2_q), .in3(t3_q), .in4(t4_q), .in5(zero_q), .in6(sp_q), .in7(t0_q),
    .out(Read_Data_1), .sel(SrcReg1[2:0]));
  Register #(.width(4)) zero (.D(and_1_out), .Q(zero_q), .clk(demultiplexer_1_out0));  // open: en, clr
  assign and_2_out = Dst_Reg_1[2:0] & {3{RegWrite}};  // AND_Gate and_2, 3 bits wide
  Register #(.width(4)) t1 (.D(WriteData), .en(demultiplexer_1_out1), .Q(t1_q), .clk(CLK), .clr(CLR));
  Register #(.width(4)) t2 (.D(WriteData), .en(demultiplexer_1_out2), .Q(t2_q), .clk(CLK), .clr(CLR));
  Demultiplexer #(.select(3), .enable("false")) demultiplexer_1 (
    .out0(demultiplexer_1_out0), .out1(demultiplexer_1_out1), .out2(demultiplexer_1_out2),
    .out3(demultiplexer_1_out3), .out4(demultiplexer_1_out4), .out6(demultiplexer_1_out6),
    .out7(demultiplexer_1_out7), .in(RegWrite), .sel(and_2_out));  // open: out5
  Register #(.width(4)) t3 (.D(WriteData), .en(demultiplexer_1_out3), .Q(t3_q), .clk(CLK), .clr(CLR));
  Register #(.width(4)) t4 (.D(WriteData), .en(demultiplexer_1_out4), .Q(t4_q), .clk(CLK), .clr(CLR));
  Register #(.width(4)) t0 (.D(WriteData), .en(demultiplexer_1_out7), .Q(t0_q), .clk(CLK), .clr(CLR));
  Multiplexer #(.select(3), .width(4), .enable("false")) multiplexer_2 (
    .in0(zero_q), .in1(t1_q), .in2(t2_q), .in3(t3_q), .in4(t4_q), .in5(zero_q), .in6(sp_q), .in7(t0_q),
    .out(Read_Data_2), .sel(SrcReg2[2:0]));
  Register #(.width(4)) sp (.D(WriteData), .en(demultiplexer_1_out6), .Q(sp_q), .clk(CLK), .clr(CLR));
endmodule
