// Logisim project b2_grp_4.circ as structural Verilog: 6 circuits, main circuit main
module main (
  input  in_1,
  output [3:0] sp,
  output [3:0] t0,
  output [3:0] t1,
  output [3:0] t2,
  output [3:0] out_6,
  output [3:0] t3,
  output [3:0] t4
);

  wire alu_1_zero_flag, clock_1_out, control_1_alusrc, control_1_beq, control_1_bneq, control_1_jump,
       control_1_memread, control_1_memtoreg, control_1_memwrite, control_1_regdst, control_1_regwrite,
       multiplexer_4_out;
  wire [2:0] control_1_alu;
  wire [3:0] alu_1_output, data_stack_memory_1_data_read, instruction_1__0_3, instruction_1__4_7,
       instruction_1__8_11, instruction_1_opcode, multiplexer_1_out, multiplexer_2_out, multiplexer_6_out,
       registers_1_read_data_1, registers_1_read_data_2;
  wire [7:0] adder_1_out, adder_2_out, bit_extender_1_out, instruction_1_jmpaddr, instruction_1_pc_read,
       multiplexer_3_out, multiplexer_5_out;

  Clock clock_1 (.out(clock_1_out));
  Adder adder_1 (.a(instruction_1_pc_read), .b(8'h1), .out(adder_1_out));  // open: cin, cout
  Instruction instruction_1 (
    .PC_Write(multiplexer_5_out), .Clock(clock_1_out), .Reset(in_1), .Opcode(instruction_1_opcode),
    ._8_11(instruction_1__8_11), ._4_7(instruction_1__4_7), ._0_3(instruction_1__0_3),
    .JmpAddr(instruction_1_jmpaddr), .PC_Read(instruction_1_pc_read));
  assign bit_extender_1_out = {{4{instruction_1__0_3[3]}}, instruction_1__0_3};  // Bit_Extender bit_extender_1
  Multiplexer #(.width(4), .enable("false")) multiplexer_1 (
    .in0(instruction_1__4_7), .in1(instruction_1__0_3), .out(multiplexer_1_out), .sel(control_1_regdst));
  Adder adder_2 (.a(bit_extender_1_out), .b(adder_1_out), .out(adder_2_out));  // open: cin, cout
  Control control_1 (
    .OP_Code(instruction_1_opcode), .ALU(control_1_alu), .RegDst(control_1_regdst),
    .ALUSrc(control_1_alusrc), .MemToReg(control_1_memtoreg), .RegWrite(control_1_regwrite),
    .MemRead(control_1_memread), .MemWrite(control_1_memwrite), .beq(control_1_beq), .bneq(control_1_bneq),
    .Jump(control_1_jump));
  Registers registers_1 (
    .RegWrite(control_1_regwrite), .CLR(in_1), .WriteData(multiplexer_6_out), .Dst_Reg_1(multiplexer_1_out),
    .sp__t4__t3__t2__t1__t0({sp, t4, t3, t2, t1, t0}), .CLK(clock_1_out), .SrcReg1(instruction_1__8_11),
    .SrcReg2(instruction_1__4_7), .Read_Data_1(registers_1_read_data_1), .Read_Data_2(registers_1_read_data_2));
  Multiplexer #(.width(4), .enable("false")) multiplexer_2 (
    .in0(registers_1_read_data_2), .in1(instruction_1__0_3), .out(multiplexer_2_out), .sel(control_1_alusrc));
  Multiplexer #(.width(8), .enable("false")) multiplexer_3 (
    .in0(adder_1_out), .in1(adder_2_out), .out(multiplexer_3_out), .sel(multiplexer_4_out));
  Multiplexer #(.enable("false")) multiplexer_4 (
    .in0(control_1_bneq), .in1(control_1_beq), .out(multiplexer_4_out), .sel(alu_1_zero_flag));
  ALU alu_1 (
    .ALU(control_1_alu), .A(registers_1_read_data_1), .B(multiplexer_2_out), .Output(alu_1_output),
    .Zero_flag(alu_1_zero_flag));
  Multiplexer #(.width(8), .enable("false")) multiplexer_5 (
    .in0(multiplexer_3_out), .in1(instruction_1_jmpaddr), .out(multiplexer_5_out), .sel(control_1_jump));
  Data_Stack_Memory data_stack_memory_1 (
    .Address(alu_1_output), .Write_Data(registers_1_read_data_2), .CLK(clock_1_out),
    .Data_Read(data_stack_memory_1_data_read), .MemRead(control_1_memread), .MemWrite(control_1_memwrite),
    .CLR(in_1));
  Multiplexer #(.width(4), .enable("false")) multiplexer_6 (
    .in0(alu_1_output), .in1(data_stack_memory_1_data_read), .out(multiplexer_6_out), .sel(control_1_memtoreg));
  RAM #(.addrWidth(4), .dataWidth(4), .bus("separate")) ram_1 (
    .addr(alu_1_output), .din(registers_1_read_data_2), .data(out_6), .str(control_1_memwrite),
    .clk(clock_1_out), .ld(control_1_memread), .clr(in_1));  // open: sel

  // Notes on the sheet:
  //   Stack Memory Visualization
endmodule

module Registers (
  input  RegWrite,
  input  CLR,
  input  [3:0] WriteData,
  input  [3:0] Dst_Reg_1,
  input  CLK,
  input  [3:0] SrcReg1,
  input  [3:0] SrcReg2,
  output [23:0] sp__t4__t3__t2__t1__t0,
  output [3:0] Read_Data_1,
  output [3:0] Read_Data_2
);

  wire demultiplexer_1_out0, demultiplexer_1_out1, demultiplexer_1_out2, demultiplexer_1_out3,
       demultiplexer_1_out4, demultiplexer_1_out6, demultiplexer_1_out7;
  wire [2:0] and_2_out;
  wire [3:0] and_1_out, zero_q;

  assign and_1_out = 4'b0000 & WriteData;  // AND_Gate and_1, 4 bits wide
  Multiplexer #(.select(3), .width(4), .enable("false")) multiplexer_1 (
    .in0(zero_q), .in1(sp__t4__t3__t2__t1__t0[7:4]), .in2(sp__t4__t3__t2__t1__t0[11:8]),
    .in3(sp__t4__t3__t2__t1__t0[15:12]), .in4(sp__t4__t3__t2__t1__t0[19:16]), .in5(zero_q),
    .in6(sp__t4__t3__t2__t1__t0[23:20]), .in7(sp__t4__t3__t2__t1__t0[3:0]), .out(Read_Data_1),
    .sel(SrcReg1[2:0]));
  Register #(.width(4)) zero (.D(and_1_out), .Q(zero_q), .clk(demultiplexer_1_out0), .clr(CLR));  // open: en
  assign and_2_out = Dst_Reg_1[2:0] & {3{RegWrite}};  // AND_Gate and_2, 3 bits wide
  Register #(.width(4)) t1 (
    .D(WriteData), .en(demultiplexer_1_out1), .Q(sp__t4__t3__t2__t1__t0[7:4]), .clk(CLK), .clr(CLR));
  Register #(.width(4)) t2 (
    .D(WriteData), .en(demultiplexer_1_out2), .Q(sp__t4__t3__t2__t1__t0[11:8]), .clk(CLK), .clr(CLR));
  Register #(.width(4)) t3 (
    .D(WriteData), .en(demultiplexer_1_out3), .Q(sp__t4__t3__t2__t1__t0[15:12]), .clk(CLK), .clr(CLR));
  Demultiplexer #(.select(3), .enable("false")) demultiplexer_1 (
    .out0(demultiplexer_1_out0), .out1(demultiplexer_1_out1), .out2(demultiplexer_1_out2),
    .out3(demultiplexer_1_out3), .out4(demultiplexer_1_out4), .out6(demultiplexer_1_out6),
    .out7(demultiplexer_1_out7), .in(RegWrite), .sel(and_2_out));  // open: out5
  Register #(.width(4)) t4 (
    .D(WriteData), .en(demultiplexer_1_out4), .Q(sp__t4__t3__t2__t1__t0[19:16]), .clk(CLK), .clr(CLR));
  Register #(.width(4)) t0 (
    .D(WriteData), .en(demultiplexer_1_out7), .Q(sp__t4__t3__t2__t1__t0[3:0]), .clk(CLK), .clr(CLR));
  Multiplexer #(.select(3), .width(4), .enable("false")) multiplexer_2 (
    .in0(zero_q), .in1(sp__t4__t3__t2__t1__t0[7:4]), .in2(sp__t4__t3__t2__t1__t0[11:8]),
    .in3(sp__t4__t3__t2__t1__t0[15:12]), .in4(sp__t4__t3__t2__t1__t0[19:16]), .in5(zero_q),
    .in6(sp__t4__t3__t2__t1__t0[23:20]), .in7(sp__t4__t3__t2__t1__t0[3:0]), .out(Read_Data_2),
    .sel(SrcReg2[2:0]));
  Register #(.width(4)) sp (
    .D(WriteData), .en(demultiplexer_1_out6), .Q(sp__t4__t3__t2__t1__t0[23:20]), .clk(CLK), .clr(CLR));
endmodule

module Instruction (
  input  [7:0] PC_Write,
  input  Clock,
  input  Reset,
  output [7:0] PC_Read,
  output [3:0] Opcode,
  output [3:0] _8_11,
  output [3:0] _4_7,
  output [3:0] _0_3,
  output [7:0] JmpAddr
);

  Register #(.trigger("falling")) PC (.D(PC_Write), .Q(PC_Read), .clk(Clock), .clr(Reset));  // open: en
  ROM #(.dataWidth(16)) rom_1 (.addr(PC_Read), .data({Opcode, _8_11, _4_7, _0_3}), .sel(1'b1));

  assign JmpAddr = {_8_11, _4_7};

  // Notes on the sheet:
  //   contents of rom_1 (hex, n*v repeats v):
  //   e06f e060 e071 e661 6670 e072 e661 6670 e071 e661 6670 e072 e661 6670 e010 e020 e044 1425 4630 e66f
  //   f131 e221 8110
endmodule

module Data_Stack_Memory (
  input  MemRead,
  input  MemWrite,
  input  [3:0] Address,
  input  [3:0] Write_Data,
  input  CLK,
  input  CLR,
  output [3:0] Data_Read
);

  wire not_1_out;

  not not_1 (not_1_out, CLK);
  RAM #(.addrWidth(4), .dataWidth(4), .bus("separate")) ram_1 (
    .addr(Address), .din(Write_Data), .data(Data_Read), .str(MemWrite), .clk(not_1_out), .ld(MemRead),
    .clr(CLR));  // open: sel
endmodule

module ALU (
  input  [2:0] ALU,
  input  [3:0] A,
  input  [3:0] B,
  output [3:0] Output,
  output Zero_flag
);

  wire [3:0] adder_1_out, and_1_out, nor_1_out, or_1_out, shifter_1_out, shifter_2_out, subtractor_1_out;

  Adder #(.width(4)) adder_1 (.a(A), .b(B), .out(adder_1_out), .cin(1'b0));  // open: cout
  Subtractor #(.width(4)) subtractor_1 (.a(A), .b(B), .out(subtractor_1_out), .bin(1'b0));  // open: bout
  assign and_1_out = A & B;  // AND_Gate and_1, 4 bits wide
  assign or_1_out = A | B;  // OR_Gate or_1, 4 bits wide
  assign nor_1_out = ~(A | B);  // NOR_Gate nor_1, 4 bits wide
  Shifter #(.width(4)) shifter_1 (.in(A), .\dist (B[1:0]), .out(shifter_1_out));
  Shifter #(.width(4), .shift("lr")) shifter_2 (.in(A), .\dist (B[1:0]), .out(shifter_2_out));
  Multiplexer #(.select(3), .width(4), .enable("false")) multiplexer_1 (
    .in0(adder_1_out), .in1(subtractor_1_out), .in2(and_1_out), .in3(or_1_out), .in4(nor_1_out),
    .in5(shifter_1_out), .in6(shifter_2_out), .in7(4'b0000), .out(Output), .sel(ALU));
  nor nor_2 (Zero_flag, Output[0], Output[1], Output[2], Output[3]);
endmodule

module Control (
  input  [3:0] OP_Code,
  output [2:0] ALU,
  output Jump,
  output bneq,
  output beq,
  output MemWrite,
  output MemRead,
  output RegWrite,
  output MemToReg,
  output ALUSrc,
  output RegDst
);

  ROM #(.addrWidth(4), .dataWidth(12)) rom_1 (
    .addr(OP_Code), .data({RegDst, ALUSrc, MemToReg, RegWrite, MemRead, MemWrite, beq, bneq, Jump, ALU}));  // open: sel

  // Notes on the sheet:
  //   contents of rom_1 (hex, n*v repeats v):
  //   903 21 901 502 780 505 640 902 8 506 501 904 503 11 500 900
endmodule
