// Logisim project B2_Grp-4.circ as structural Verilog
module Instruction_Memory (
  input  [3:0] PC,
  output [15:0] Instruction_0___15
);

  ROM #(.addrWidth(4), .dataWidth(16)) rom_1 (.addr(PC), .data(Instruction_0___15));  // open: sel
endmodule

module main (
  input  [3:0] PC,
  output [15:0] Instruction_set
);

  Instruction_Memory Ins_Mem (.PC(PC), .Instruction_0___15(Instruction_set));
endmodule
